# Fritzing sketch ESP MQTT Digital LEDs Wiring Diagram (saved by Fritzing 0.9.3b)
perfboards: 1

parts:
  U1 = NodeMCU V1.0
  5V = Power plug
  NEOPIXEL1 = Neopixel Strip -- Black (30/m)
  NEOPIXEL2 = Neopixel Strip -- Black (30/m)  # not connected
  NEOPIXEL3 = Neopixel Strip -- Black (30/m)  # not connected
  S1 = SWITCH-MOMENTARY-2 [package=tactile-switch-1101ne]

nets:
  N1: U1.D3, S1.2
  VCC: 5V.VCC, NEOPIXEL1.+5V
  N2: 5V.GND, S1.1

custom parts:
  NodeMCU V1.0: ESP8266 based NodeMCU
  Neopixel Strip -- Black (30/m): These NeoPixel strips have 30 digitally-addressable pixel LEDs per meter and are very affordable and are only 12.5 mm wide, 10 mm if you remove the strip from the casing.
